// Logisim project syn01.circ as structural Verilog: 23 circuits, main circuit main
module main (
  input  in_1,
  output [7:0] ADDR,
  output [7:0] DATA
);

  wire button_1_out, button_2_out, syn_01_1_ale, syn_01_1_clk, syn_01_1_rd, syn_01_1_wr;
  wire [7:0] ppi_1_p0, ppi_1_p1, ppi_1_p2, ppi_1_p3, ppi_2_p0, ppi_2_p1, ppi_2_p2, ppi_2_p3;

  Button button_1 (.out(button_1_out));
  Button button_2 (.out(button_2_out));
  SYN_01 syn_01_1 (
    .D_IN(DATA), .STEP(button_1_out), .CLK_MODE(in_1), .RESET(button_2_out), .AD_OUT(DATA),
    .CLK(syn_01_1_clk), .RD(syn_01_1_rd), .WR(syn_01_1_wr), .ALE(syn_01_1_ale));
  Register register_1 (.D(DATA), .en(syn_01_1_ale), .clk(syn_01_1_clk), .Q(ADDR), .clr(button_2_out));
  RAM ram_1 (.addr(ADDR), .we(syn_01_1_wr), .oe(syn_01_1_rd), .clk(syn_01_1_clk), .data(DATA));
  PPI ppi_1 (
    .D_IN(DATA), .MEM_ADDR(ADDR), .PPI_ADDR(8'hfe), .OE(syn_01_1_wr), .CLK(syn_01_1_clk), .MR(button_2_out),
    .P0(ppi_1_p0), .P1(ppi_1_p1), .P2(ppi_1_p2), .P3(ppi_1_p3));
  PPI ppi_2 (
    .D_IN(DATA), .MEM_ADDR(ADDR), .PPI_ADDR({8{1'b1}}), .OE(syn_01_1_wr), .CLK(syn_01_1_clk),
    .MR(button_2_out), .P0(ppi_2_p0), .P1(ppi_2_p1), .P2(ppi_2_p2), .P3(ppi_2_p3));
  DotMatrix #(.matrixcols(8), .matrixrows(8)) dotmatrix_1 (
    .col0(ppi_1_p0), .col1(ppi_1_p1), .col2(ppi_1_p2), .col3(ppi_1_p3), .col4(ppi_2_p0), .col5(ppi_2_p1),
    .col6(ppi_2_p2), .col7(ppi_2_p3));
endmodule

module TIMING_MODULE (
  input  STEP,
  input  CLK_MODE,
  input  HLT,
  output SYS_CLK,
  output NEG_SYS_CLK
);

  wire clock_1_out, multiplexer_1_out, not_1_out, not_2_out;

  Clock clock_1 (.out(clock_1_out));
  Multiplexer #(.enable("false")) multiplexer_1 (
    .in0(clock_1_out), .in1(STEP), .out(multiplexer_1_out), .sel(CLK_MODE));
  not not_1 (not_1_out, multiplexer_1_out);
  not not_2 (not_2_out, HLT);
  and and_1 (SYS_CLK, multiplexer_1_out, not_2_out);
  and and_2 (NEG_SYS_CLK, not_1_out, not_2_out);
endmodule

module TIMING_MODULE_test (
  input  in_1,
  input  in_2,
  output out_3,
  output out_4
);

  wire button_1_out;

  Button button_1 (.out(button_1_out));
  TIMING_MODULE timing_module_1 (
    .STEP(button_1_out), .CLK_MODE(in_1), .HLT(in_2), .SYS_CLK(out_3), .NEG_SYS_CLK(out_4));
endmodule

module REG_8 (
  input  [7:0] R_D,
  input  R_LD,
  input  R_OE,
  input  CLK,
  input  MR,
  output [7:0] R_Q
);

  wire [7:0] R_q_2;

  Register R (.D(R_D), .en(R_LD), .clk(CLK), .Q(R_q_2), .clr(MR));
  assign R_Q = R_OE ? R_q_2 : 8'bz;  // Controlled_Buffer controlled_buffer_1
endmodule

module REG_16 (
  input  [7:0] R_D,
  input  RH_LD,
  input  RL_LD,
  input  RH_OE,
  input  RL_OE,
  input  CLK,
  input  MR,
  output [7:0] R_Q
);

  REG_8 RH (.R_D(R_D), .R_LD(RH_LD), .R_OE(RH_OE), .CLK(CLK), .MR(MR), .R_Q(R_Q));
  REG_8 RL (.R_D(R_D), .R_LD(RL_LD), .R_OE(RL_OE), .CLK(CLK), .MR(MR), .R_Q(R_Q));
endmodule

module REG_X_test (
  input  [7:0] in_1,
  input  in_2,
  input  in_3,
  input  in_4,
  input  in_5,
  input  [7:0] in_6,
  input  in_7,
  input  in_8,
  input  in_9,
  input  in_10,
  input  in_11,
  input  in_12,
  output [7:0] out_13,
  output [7:0] out_14
);

  REG_8 reg_8_1 (.R_D(in_1), .R_LD(in_2), .R_OE(in_3), .CLK(in_4), .MR(in_5), .R_Q(out_13));
  REG_16 reg_16_1 (
    .R_D(in_6), .RH_LD(in_7), .RL_LD(in_8), .RH_OE(in_9), .RL_OE(in_10), .CLK(in_11), .MR(in_12), .R_Q(out_14));
endmodule

module REG_8x4 (
  input  [7:0] R_D,
  input  R0_LD,
  input  R1_LD,
  input  R2_LD,
  input  R3_LD,
  input  R0_OE,
  input  R1_OE,
  input  R2_OE,
  input  R3_OE,
  input  CLK,
  input  MR,
  output [7:0] R_Q
);

  REG_16 R02 (.R_D(R_D), .RH_LD(R0_LD), .RL_LD(R2_LD), .RH_OE(R0_OE), .RL_OE(R2_OE), .CLK(CLK), .MR(MR), .R_Q(R_Q));
  REG_16 R13 (.R_D(R_D), .RH_LD(R1_LD), .RL_LD(R3_LD), .RH_OE(R1_OE), .RL_OE(R3_OE), .CLK(CLK), .MR(MR), .R_Q(R_Q));
endmodule

module REG_8x4_test (
  input  [7:0] in_1,
  input  in_2,
  input  [3:0] in_3,
  input  [3:0] in_4,
  input  in_5,
  output [7:0] out_6
);

  wire clock_1_out;

  assign out_6 = in_2 ? in_1 : 8'bz;  // Controlled_Buffer controlled_buffer_1
  Clock clock_1 (.out(clock_1_out));
  REG_8x4 reg_8x4_1 (
    .R_D(out_6), .R0_LD(in_3[0]), .R1_LD(in_3[1]), .R2_LD(in_3[2]), .R3_LD(in_3[3]), .R0_OE(in_4[0]),
    .R1_OE(in_4[1]), .R2_OE(in_4[2]), .R3_OE(in_4[3]), .CLK(clock_1_out), .MR(in_5), .R_Q(out_6));
endmodule

module IP (
  input  [7:0] IP_D,
  input  IP_LD,
  input  IP_OE,
  input  IP_INC,
  input  CLK,
  input  MR,
  output [7:0] IP_Q
);

  wire [7:0] counter_1_q;

  Counter counter_1 (
    .clr(MR), .load(IP_LD), .up(1'b1), .count(IP_INC), .clk(CLK), .D(IP_D), .Q(counter_1_q));  // open: carry
  assign IP_Q = IP_OE ? counter_1_q : 8'bz;  // Controlled_Buffer controlled_buffer_1
endmodule

module IP_test (
  input  [7:0] in_1,
  input  in_2,
  input  in_3,
  input  in_4,
  input  in_5,
  input  in_6,
  input  in_7,
  input  in_8,
  input  in_9,
  input  in_10,
  input  in_11,
  input  in_12,
  input  in_13,
  output [7:0] out_14
);

  wire button_1_out, timing_module_1_sys_clk;

  Button button_1 (.out(button_1_out));
  assign out_14 = in_2 ? in_1 : 8'bz;  // Controlled_Buffer controlled_buffer_1
  TIMING_MODULE timing_module_1 (
    .STEP(button_1_out), .CLK_MODE(in_12), .HLT(in_13), .SYS_CLK(timing_module_1_sys_clk));  // open: NEG_SYS_CLK
  IP ip_1 (
    .IP_D(out_14), .IP_LD(in_4), .IP_OE(in_6), .IP_INC(in_8), .CLK(timing_module_1_sys_clk), .MR(in_10),
    .IP_Q(out_14));
  REG_16 reg_16_1 (
    .R_D(out_14), .RH_LD(in_3), .RL_LD(in_5), .RH_OE(in_7), .RL_OE(in_9), .CLK(timing_module_1_sys_clk),
    .MR(in_11), .R_Q(out_14));
endmodule

module ALU_REG (
  input  [7:0] AR_D,
  input  CY_D,
  input  CY_LD,
  input  AR0_LD,
  input  AR1_LD,
  input  CLK,
  input  MR,
  output [7:0] AR0_Q,
  output [7:0] AR1_Q,
  output CY_Q
);

  assign CY_Q = CY_LD ? CY_D : 1'bz;  // Controlled_Buffer controlled_buffer_1
  Register register_1 (.D(AR_D), .en(AR0_LD), .clk(CLK), .Q(AR0_Q), .clr(MR));
  Register register_2 (.D(AR_D), .en(AR1_LD), .clk(CLK), .Q(AR1_Q), .clr(MR));
endmodule

module ALU_AS (
  input  [7:0] ALU_AS_R0,
  input  [7:0] ALU_AS_R1,
  input  F_SEL,
  input  CY_D,
  input  ALU_AS_OE,
  output [7:0] AS_Q,
  output CY_Q
);

  wire adder_1_cout, subtractor_1_bout;
  wire [7:0] adder_1_out, subtractor_1_out;

  Adder adder_1 (.a(ALU_AS_R0), .b(ALU_AS_R1), .out(adder_1_out), .cin(CY_D), .cout(adder_1_cout));
  Subtractor subtractor_1 (.a(ALU_AS_R0), .b(ALU_AS_R1), .out(subtractor_1_out), .bin(CY_D), .bout(subtractor_1_bout));
  Multiplexer #(.width(8), .disabled("Z")) multiplexer_1 (
    .in0(adder_1_out), .in1(subtractor_1_out), .out(AS_Q), .sel(F_SEL), .en(ALU_AS_OE));
  Multiplexer #(.disabled("Z")) multiplexer_2 (
    .in0(adder_1_cout), .in1(subtractor_1_bout), .out(CY_Q), .sel(F_SEL), .en(ALU_AS_OE));
endmodule

module ALU_LG (
  input  [7:0] ALU_LG_R0,
  input  [7:0] ALU_LG_R1,
  input  [1:0] F_SEL,
  input  ALU_LG_OE,
  output [7:0] LG_Q
);

  wire [7:0] and_1_out, not_1_out, or_1_out, xor_1_out;

  assign not_1_out = ~ALU_LG_R0;  // NOT_Gate not_1, 8 bits wide
  assign and_1_out = ALU_LG_R0 & ALU_LG_R1;  // AND_Gate and_1, 8 bits wide
  assign or_1_out = ALU_LG_R0 | ALU_LG_R1;  // OR_Gate or_1, 8 bits wide
  assign xor_1_out = ALU_LG_R0 ^ ALU_LG_R1;  // XOR_Gate xor_1, 8 bits wide
  Multiplexer #(.select(2), .width(8), .disabled("Z")) multiplexer_1 (
    .in0(not_1_out), .in1(and_1_out), .in2(or_1_out), .in3(xor_1_out), .out(LG_Q), .sel(F_SEL), .en(ALU_LG_OE));
endmodule

module ALU (
  input  [7:0] AR_D,
  input  CY_D,
  input  CY_LD,
  input  AR0_LD,
  input  AR1_LD,
  input  F_SEL_A2,
  input  F_SEL_A1,
  input  F_SEL_A0,
  input  ALU_AS_OE,
  input  ALU_LG_OE,
  input  CLK,
  input  MR,
  output [7:0] ALU_Q,
  output CY_Q
);

  wire alu_reg_1_cy_q;
  wire [7:0] alu_reg_1_ar0_q, alu_reg_1_ar1_q;

  ALU_REG alu_reg_1 (
    .AR_D(AR_D), .CY_D(CY_D), .CY_LD(CY_LD), .AR0_LD(AR0_LD), .AR1_LD(AR1_LD), .CLK(CLK), .MR(MR),
    .AR0_Q(alu_reg_1_ar0_q), .AR1_Q(alu_reg_1_ar1_q), .CY_Q(alu_reg_1_cy_q));
  ALU_AS alu_as_1 (
    .ALU_AS_R0(alu_reg_1_ar0_q), .ALU_AS_R1(alu_reg_1_ar1_q), .F_SEL(F_SEL_A0), .CY_D(alu_reg_1_cy_q),
    .ALU_AS_OE(ALU_AS_OE), .AS_Q(ALU_Q), .CY_Q(CY_Q));
  ALU_LG alu_lg_1 (
    .ALU_LG_R0(alu_reg_1_ar0_q), .ALU_LG_R1(alu_reg_1_ar1_q), .F_SEL({F_SEL_A2, F_SEL_A1}),
    .ALU_LG_OE(ALU_LG_OE), .LG_Q(ALU_Q));
endmodule

module ALU_test (
  input  [7:0] in_1,
  input  in_2,
  input  in_3,
  input  in_4,
  input  in_5,
  input  in_6,
  input  in_7,
  input  in_8,
  input  in_9,
  input  in_10,
  input  in_11,
  input  in_12,
  output [7:0] out_13
);

  wire button_1_out, timing_module_1_sys_clk;

  Button button_1 (.out(button_1_out));
  assign out_13 = in_2 ? in_1 : 8'bz;  // Controlled_Buffer controlled_buffer_1
  TIMING_MODULE timing_module_1 (
    .STEP(button_1_out), .CLK_MODE(in_10), .HLT(in_12), .SYS_CLK(timing_module_1_sys_clk));  // open: NEG_SYS_CLK
  ALU alu_1 (
    .AR_D(out_13), .AR0_LD(in_3), .AR1_LD(in_4), .F_SEL_A2(in_5), .F_SEL_A1(in_6), .F_SEL_A0(in_7),
    .ALU_AS_OE(in_8), .ALU_LG_OE(in_9), .CLK(timing_module_1_sys_clk), .MR(in_11), .ALU_Q(out_13));  // open: CY_D, CY_LD, CY_Q
endmodule

module T_ST_CNTR (
  input  CLK,
  input  MR,
  output [3:0] T_Q
);

  Counter #(.width(4), .max('hf)) counter_1 (
    .clr(MR), .load(1'b0), .up(1'b1), .count(1'b1), .clk(CLK), .Q(T_Q));  // open: D, carry
endmodule

module T_ST_CNTR_test (
  input  in_1,
  input  in_2,
  input  in_3,
  output [3:0] out_4
);

  wire button_1_out, timing_module_1_neg_sys_clk;

  Button button_1 (.out(button_1_out));
  TIMING_MODULE timing_module_1 (
    .STEP(button_1_out), .CLK_MODE(in_1), .HLT(in_2), .NEG_SYS_CLK(timing_module_1_neg_sys_clk));  // open: SYS_CLK
  T_ST_CNTR t_st_cntr_1 (.CLK(timing_module_1_neg_sys_clk), .MR(in_3), .T_Q(out_4));
endmodule

module HW_FC (
  input  [7:0] T_ST_D,
  output [7:0] T_ST_Q,
  output IDR_OE,
  output IP_OE,
  output ALE,
  output RD,
  output IDR_LD,
  output IP_INC
);

  wire not_1_out;
  wire [7:0] subtractor_1_out;

  Subtractor subtractor_1 (.a(T_ST_D), .b(8'h3), .out(subtractor_1_out));  // open: bin, bout
  Comparator comparator_1 (.a(T_ST_D), .b(8'h2), .gt(IDR_OE));  // open: eq, lt
  assign T_ST_Q = IDR_OE ? subtractor_1_out : 8'bz;  // Controlled_Buffer controlled_buffer_1
  not not_1 (not_1_out, IDR_OE);
  Decoder #(.select(3), .tristate("true"), .disabled("Z")) decoder_1 (
    .out0(ALE), .out2(IDR_LD), .sel(T_ST_D[2:0]), .en(not_1_out));  // open: out1, out3, out4, out5, out6, out7

  assign IP_INC = IDR_LD;
  assign IP_OE = ALE;
  assign RD = IDR_LD;
endmodule

module MC_L_ROM (
  input  [3:0] T_ST_D,
  input  [7:0] IDR_D,
  output HLT,
  output IDR_LD,
  output IDR_OE,
  output IP_LD,
  output IP_OE,
  output IP_INC,
  output MAR_LD,
  output MAR_OE,
  output R0_LD,
  output R0_OE,
  output R1_LD,
  output R1_OE,
  output R2_LD,
  output R2_OE,
  output R3_LD,
  output R3_OE,
  output AR0_LD,
  output AR1_LD,
  output ALU_AS_OE,
  output F_SEL_A0,
  output MR,
  output T_ST_MR,
  output RD,
  output WR,
  output ALE
);

  ROM #(.addrWidth(12), .dataWidth(24)) rom_1 (
    .addr({IDR_D, T_ST_D}),
    .data({ALE, WR, RD, T_ST_MR, MR, F_SEL_A0, ALU_AS_OE, AR1_LD, AR0_LD, R3_OE, R3_LD, R2_OE, R2_LD, R1_OE, R1_LD, R0_OE, R0_LD, MAR_OE, MAR_LD, IP_INC, IP_OE, IP_LD, IDR_LD, HLT}));
  Comparator #(.width(4), .mode("unsigned")) comparator_1 (.a(T_ST_D), .b(4'b0001), .gt(IDR_OE));  // open: eq, lt

  // Notes on the sheet:
  //   contents of rom_1 (hex, n*v repeats v):
  //   800008 0 200012 0 100000 11*0 800008 0 200012 1 12*0 800008 0 200012 480 100000 11*0 800008 0 200012
  //   1080 100000 11*0 800008 0 200012 4080 100000 11*0 800008 0 200012 300 100000 11*0 800008 0 200012
  //   1200 100000 11*0 800008 0 200012 4200 100000 11*0 800008 0 200012 900 100000 11*0 800008 0 200012
  //   c00 100000 11*0 800008 0 200012 4800 100000 11*0 800008 0 200012 2100 100000 11*0 800008 0 200012
  //   2400 100000 11*0 800008 0 200012 3000 100000 11*0 800008 0 200012 800018 0 200080 100000 9*0 800008
  //   0 200012 800018 0 200200 100000 9*0 800008 0 200012 800018 0 200800 100000 9*0 800008 0 200012
  //   800018 0 202000 100000 9*0 800008 0 200012 800018 0 a00000 0 200080 100000 7*0 800008 0 200012
  //   800018 0 a00000 0 200200 100000 7*0 800008 0 200012 800018 0 a00000 0 200800 100000 7*0 800008 0
  //   200012 800018 0 a00000 0 202000 100000 7*0 800008 0 200012 800018 0 a00000 400100 100000 8*0 800008
  //   0 200012 800018 0 a00000 400400 100000 8*0 800008 0 200012 800018 0 a00000 401000 100000 8*0 800008
  //   0 200012 800018 0 a00000 404000 100000 8*0 800008 0 200012 800008 0 200004 100000 9*0 800008 0
  //   200012 800018 0 210000 8100 20080 100000
endmodule

module SYN_01 (
  input  [7:0] D_IN,
  input  STEP,
  input  CLK_MODE,
  input  RESET,
  output [7:0] AD_OUT,
  output CLK,
  output RD,
  output WR,
  output ALE
);

  wire mc_l_rom_1_alu_as_oe, mc_l_rom_1_ar0_ld, mc_l_rom_1_ar1_ld, mc_l_rom_1_f_sel_a0, mc_l_rom_1_hlt,
       mc_l_rom_1_idr_ld, mc_l_rom_1_idr_oe, mc_l_rom_1_ip_inc, mc_l_rom_1_ip_ld, mc_l_rom_1_ip_oe,
       mc_l_rom_1_mar_ld, mc_l_rom_1_mar_oe, mc_l_rom_1_mr, mc_l_rom_1_r0_ld, mc_l_rom_1_r0_oe,
       mc_l_rom_1_r1_ld, mc_l_rom_1_r1_oe, mc_l_rom_1_r2_ld, mc_l_rom_1_r2_oe, mc_l_rom_1_r3_ld,
       mc_l_rom_1_r3_oe, mc_l_rom_1_t_st_mr, not_1_out, or_1_out, or_2_out, timing_module_1_neg_sys_clk;
  wire [3:0] t_st_cntr_1_t_q;
  wire [7:0] IDR_r_q, MAR_r_q;

  or or_1 (or_1_out, RESET, mc_l_rom_1_mr);
  TIMING_MODULE timing_module_1 (
    .STEP(STEP), .CLK_MODE(CLK_MODE), .HLT(mc_l_rom_1_hlt), .SYS_CLK(CLK),
    .NEG_SYS_CLK(timing_module_1_neg_sys_clk));
  or or_2 (or_2_out, or_1_out, mc_l_rom_1_t_st_mr);
  T_ST_CNTR t_st_cntr_1 (.CLK(timing_module_1_neg_sys_clk), .MR(or_2_out), .T_Q(t_st_cntr_1_t_q));
  MC_L_ROM mc_l_rom_1 (
    .T_ST_D(t_st_cntr_1_t_q), .IDR_D(IDR_r_q), .HLT(mc_l_rom_1_hlt), .IDR_LD(mc_l_rom_1_idr_ld),
    .IDR_OE(mc_l_rom_1_idr_oe), .IP_LD(mc_l_rom_1_ip_ld), .IP_OE(mc_l_rom_1_ip_oe),
    .IP_INC(mc_l_rom_1_ip_inc), .MAR_LD(mc_l_rom_1_mar_ld), .MAR_OE(mc_l_rom_1_mar_oe),
    .R0_LD(mc_l_rom_1_r0_ld), .R0_OE(mc_l_rom_1_r0_oe), .R1_LD(mc_l_rom_1_r1_ld), .R1_OE(mc_l_rom_1_r1_oe),
    .R2_LD(mc_l_rom_1_r2_ld), .R2_OE(mc_l_rom_1_r2_oe), .R3_LD(mc_l_rom_1_r3_ld), .R3_OE(mc_l_rom_1_r3_oe),
    .AR0_LD(mc_l_rom_1_ar0_ld), .AR1_LD(mc_l_rom_1_ar1_ld), .ALU_AS_OE(mc_l_rom_1_alu_as_oe),
    .F_SEL_A0(mc_l_rom_1_f_sel_a0), .MR(mc_l_rom_1_mr), .T_ST_MR(mc_l_rom_1_t_st_mr), .RD(RD), .WR(WR),
    .ALE(ALE));
  REG_8 IDR (
    .R_D(MAR_r_q), .R_LD(mc_l_rom_1_idr_ld), .R_OE(mc_l_rom_1_idr_oe), .CLK(CLK), .MR(or_2_out), .R_Q(IDR_r_q));
  REG_8 MAR (
    .R_D(MAR_r_q), .R_LD(mc_l_rom_1_mar_ld), .R_OE(mc_l_rom_1_mar_oe), .CLK(CLK), .MR(or_1_out), .R_Q(MAR_r_q));
  IP ip_1 (
    .IP_D(MAR_r_q), .IP_LD(mc_l_rom_1_ip_ld), .IP_OE(mc_l_rom_1_ip_oe), .IP_INC(mc_l_rom_1_ip_inc),
    .CLK(CLK), .MR(or_1_out), .IP_Q(MAR_r_q));
  assign MAR_r_q = RD ? D_IN : 8'bz;  // Controlled_Buffer controlled_buffer_1
  REG_8x4 reg_8x4_1 (
    .R_D(MAR_r_q), .R0_LD(mc_l_rom_1_r0_ld), .R1_LD(mc_l_rom_1_r1_ld), .R2_LD(mc_l_rom_1_r2_ld),
    .R3_LD(mc_l_rom_1_r3_ld), .R0_OE(mc_l_rom_1_r0_oe), .R1_OE(mc_l_rom_1_r1_oe), .R2_OE(mc_l_rom_1_r2_oe),
    .R3_OE(mc_l_rom_1_r3_oe), .CLK(CLK), .MR(or_1_out), .R_Q(MAR_r_q));
  ALU alu_1 (
    .AR_D(MAR_r_q), .AR0_LD(mc_l_rom_1_ar0_ld), .AR1_LD(mc_l_rom_1_ar1_ld), .F_SEL_A0(mc_l_rom_1_f_sel_a0),
    .ALU_AS_OE(mc_l_rom_1_alu_as_oe), .CLK(CLK), .MR(or_1_out), .ALU_Q(MAR_r_q));  // open: CY_D, CY_LD, F_SEL_A2, F_SEL_A1, ALU_LG_OE, CY_Q
  not not_1 (not_1_out, RD);
  assign AD_OUT = not_1_out ? MAR_r_q : 8'bz;  // Controlled_Buffer controlled_buffer_2
endmodule

module SYN01_test (
  input  in_1,
  output [7:0] out_2,
  output [7:0] out_3
);

  wire bcd_to_7_segment_decoder_3_p1, binairy_to_bcd_converter_1_p2, binairy_to_bcd_converter_1_p4,
       button_1_out, button_2_out, syn_01_1_ale, syn_01_1_clk, syn_01_1_rd, syn_01_1_wr;
  wire [7:0] mem_oe_1_d_out;

  Button button_1 (.out(button_1_out));
  Button button_2 (.out(button_2_out));
  SYN_01 syn_01_1 (
    .D_IN(out_3), .STEP(button_1_out), .CLK_MODE(in_1), .RESET(button_2_out), .AD_OUT(out_3),
    .CLK(syn_01_1_clk), .RD(syn_01_1_rd), .WR(syn_01_1_wr), .ALE(syn_01_1_ale));
  Register register_1 (.D(out_3), .en(syn_01_1_ale), .clk(syn_01_1_clk), .Q(out_2), .clr(button_2_out));
  MEM_OE mem_oe_1 (
    .D_IN(out_3), .MEM_ADDR(out_2), .MEM_PORT({8{1'b1}}), .OE(syn_01_1_wr), .CLK(syn_01_1_clk),
    .MR(button_2_out), .D_OUT(mem_oe_1_d_out));
  RAM ram_1 (.addr(out_2), .we(syn_01_1_wr), .oe(syn_01_1_rd), .clk(syn_01_1_clk), .data(out_3));
  // BCD_to_7_Segment_decoder bcd_to_7_segment_decoder_1: pin names not known
  _7_Segment_Display u_7_segment_display_1 ();  // open: g, f, a, b, e, d, c, dp
  // Binairy_to_BCD_converter #(.binvalue(8)) binairy_to_bcd_converter_1: pin names not known; wires that end beside it: mem_oe_1_d_out, binairy_to_bcd_converter_1_p2, binairy_to_bcd_converter_1_p2, binairy_to_bcd_converter_1_p4
  _7_Segment_Display u_7_segment_display_2 ();  // open: g, f, a, b, e, d, c, dp
  // BCD_to_7_Segment_decoder bcd_to_7_segment_decoder_2: pin names not known; wires that end beside it: binairy_to_bcd_converter_1_p4
  _7_Segment_Display u_7_segment_display_3 ();  // open: g, f, a, b, e, d, c, dp
  // BCD_to_7_Segment_decoder bcd_to_7_segment_decoder_3: pin names not known; wires that end beside it: bcd_to_7_segment_decoder_3_p1, bcd_to_7_segment_decoder_3_p1
endmodule

module MEM_OE (
  input  [7:0] D_IN,
  input  [7:0] MEM_ADDR,
  input  [7:0] MEM_PORT,
  input  OE,
  input  CLK,
  input  MR,
  output [7:0] D_OUT
);

  wire and_1_out, comparator_1_eq;

  and and_1 (and_1_out, OE, comparator_1_eq);
  Comparator comparator_1 (.a(MEM_ADDR), .b(MEM_PORT), .eq(comparator_1_eq));  // open: gt, lt
  Register register_1 (.D(D_IN), .en(and_1_out), .clk(CLK), .Q(D_OUT), .clr(MR));
endmodule

module PPI (
  input  [7:0] D_IN,
  input  [7:0] MEM_ADDR,
  input  [7:0] PPI_ADDR,
  input  OE,
  input  CLK,
  input  MR,
  output [7:0] P0,
  output [7:0] P1,
  output [7:0] P2,
  output [7:0] P3
);

  wire [7:0] adder_1_out, adder_2_out, adder_3_out, mem_oe_1_d_out;

  MEM_OE mem_oe_1 (
    .D_IN(D_IN), .MEM_ADDR(MEM_ADDR), .MEM_PORT(PPI_ADDR), .OE(OE), .CLK(CLK), .MR(MR), .D_OUT(mem_oe_1_d_out));
  Adder adder_1 (.a(mem_oe_1_d_out), .b(8'h1), .out(adder_1_out));  // open: cin, cout
  Adder adder_2 (.a(adder_1_out), .b(8'h1), .out(adder_2_out));  // open: cin, cout
  Adder adder_3 (.a(adder_2_out), .b(8'h1), .out(adder_3_out));  // open: cin, cout
  MEM_OE mem_oe_2 (
    .D_IN(D_IN), .MEM_ADDR(MEM_ADDR), .MEM_PORT(mem_oe_1_d_out), .OE(OE), .CLK(CLK), .MR(MR), .D_OUT(P0));
  MEM_OE mem_oe_3 (.D_IN(D_IN), .MEM_ADDR(MEM_ADDR), .MEM_PORT(adder_1_out), .OE(OE), .CLK(CLK), .MR(MR), .D_OUT(P1));
  MEM_OE mem_oe_4 (.D_IN(D_IN), .MEM_ADDR(MEM_ADDR), .MEM_PORT(adder_2_out), .OE(OE), .CLK(CLK), .MR(MR), .D_OUT(P2));
  MEM_OE mem_oe_5 (.D_IN(D_IN), .MEM_ADDR(MEM_ADDR), .MEM_PORT(adder_3_out), .OE(OE), .CLK(CLK), .MR(MR), .D_OUT(P3));
endmodule
